// Logisim project MIPS_Monociclo_JAL_BGEZAL_SLTI_MULT_LUI.circ as structural Verilog: 11 circuits, main circuit main
module main (
  input  Reset,
  input  Manual,
  input  RegDst,
  input  Jump,
  input  Branch,
  input  MemRead,
  input  MemToReg,
  input  ALUop0,
  input  ALUop1,
  input  MemWrite,
  input  ALUsrc,
  input  RegWrite,
  input  WriteReg31,
  input  Bgez,
  input  Slti,
  input  LUI,
  output [2:0] ALUcontrol,
  output [5:0] funct,
  output [5:0] Opcode,
  output RegDst_2,
  output Jump_2,
  output MULT,
  output Branch_2,
  output MemRead_2,
  output MemToReg_2,
  output ALUop0_2,
  output ALUop1_2,
  output MemWrite_2,
  output ALUSrc_2,
  output RegWrite_2,
  output WriteReg31_2,
  output Bgez_2,
  output Slti_2,
  output LUI_2
);

  wire alu_1_zero, and_1_out, bitselector_1_out, ck, comparator_1_eq, comparator_1_gt, multiplexer_3_out,
       not_1_out, or_1_out;
  wire [4:0] instruction_decode_1__15_11__rd, instruction_decode_1__20_16__rt,
       instruction_decode_1__25_21__rs, multiplexer_4_out;
  wire [5:0] instruction_decode_1__31_26__opcode;
  wire [13:0] rom_1_data;
  wire [27:0] shl_26_28_1_out_2;
  wire [31:0] adder_1_out, adder_2_out, adder_3_out, alu_1_rd, and_2_out, bit_extender_1_out,
       bit_extender_2_out, HI, LO, multiplexer_5_out, multiplexer_6_out, multiplexer_7_out,
       multiplexer_8_out, multiplexer_9_out, multiplexer_10_out, PC_q, ram_1_data,
       register_bank_1_read_data_1, register_bank_1_read_data_2, rom_2_data, shl_32_1_out_2;
  wire [31:22] instruction_decode_1__15_0__shamt___funct;

  Clock Clock (.out(ck));
  Register #(.width(32)) PC (.D(multiplexer_8_out), .en(1'b1), .Q(PC_q), .clk(ck), .clr(Reset));
  not not_1 (not_1_out, Manual);
  ROM #(.addrWidth(6), .dataWidth(14)) rom_1 (.addr(Opcode), .data(rom_1_data), .sel(not_1_out));
  Comparator #(.width(32)) comparator_1 (
    .a(register_bank_1_read_data_1), .b({32{1'b0}}), .gt(comparator_1_gt), .eq(comparator_1_eq));  // open: lt
  Adder #(.width(32)) adder_1 (.a(32'h4), .b(PC_q), .out(adder_1_out));  // open: cin, cout
  ROM #(.addrWidth(24), .dataWidth(32)) rom_2 (.addr(PC_q[25:2]), .data(rom_2_data), .sel(1'b1));
  Multiplexer #(.width(14), .enable("false")) multiplexer_1 (
    .in0(rom_1_data),
    .in1({LUI, Slti, Bgez, WriteReg31, RegWrite, ALUsrc, MemWrite, ALUop1, ALUop0, MemToReg, MemRead, Branch, Jump, RegDst}),
    .out({LUI_2, Slti_2, Bgez_2, WriteReg31_2, RegWrite_2, ALUSrc_2, MemWrite_2, ALUop1_2, ALUop0_2, MemToReg_2, MemRead_2, Branch_2, Jump_2, RegDst_2}),
    .sel(Manual));
  or or_1 (or_1_out, comparator_1_gt, comparator_1_eq);
  Instruction_Decode instruction_decode_1 (
    .in_1(rom_2_data), ._31_26__OPCODE(instruction_decode_1__31_26__opcode),
    ._25_21__RS(instruction_decode_1__25_21__rs), ._20_16__RT(instruction_decode_1__20_16__rt),
    ._15_11__RD(instruction_decode_1__15_11__rd),
    ._15_0__SHAMT___FUNCT({instruction_decode_1__15_0__shamt___funct, funct}));
  Multiplexer #(.width(6)) multiplexer_2 (
    .in0(instruction_decode_1__31_26__opcode), .in1(6'b011000), .out(Opcode), .sel(MULT));  // open: en
  Multiplexer #(.enable("false")) multiplexer_3 (
    .in0(alu_1_zero), .in1(or_1_out), .out(multiplexer_3_out), .sel(Bgez_2));
  shl_26_28 shl_26_28_1 (
    .in_1({instruction_decode_1__25_21__rs, instruction_decode_1__20_16__rt, instruction_decode_1__15_0__shamt___funct, funct}),
    .out_2(shl_26_28_1_out_2));
  Multiplexer #(.select(2), .width(5)) multiplexer_4 (
    .in0(instruction_decode_1__20_16__rt), .in1(instruction_decode_1__15_11__rd), .in2({5{1'b1}}),
    .in3(5'b10001), .out(multiplexer_4_out), .sel({WriteReg31_2, RegDst_2}));  // open: en
  Register_Bank register_bank_1 (
    .Read_1_Address(instruction_decode_1__25_21__rs), .Read_2_Address(instruction_decode_1__20_16__rt),
    .Write_Address(multiplexer_4_out), .Write_Data(multiplexer_6_out), .Enable(RegWrite_2), .Reset(Reset),
    .Clock(ck), .Read_Data_1(register_bank_1_read_data_1), .Read_Data_2(register_bank_1_read_data_2));
  assign bit_extender_1_out = {{16{instruction_decode_1__15_0__shamt___funct[31]}}, {instruction_decode_1__15_0__shamt___funct, funct}};  // Bit_Extender bit_extender_1
  shl_32 shl_32_1 (.in_1(bit_extender_1_out), .out_2(shl_32_1_out_2));
  Multiplexer #(.width(32), .enable("false")) multiplexer_5 (
    .in0(register_bank_1_read_data_2), .in1(bit_extender_1_out), .out(multiplexer_5_out), .sel(ALUSrc_2));
  ALU_Control alu_control_1 (.in_1({ALUop1_2, ALUop0_2}), .in_2(funct[4:0]), .out_3(ALUcontrol));
  Adder #(.width(32)) adder_2 (.a(adder_1_out), .b(shl_32_1_out_2), .out(adder_2_out));  // open: cin, cout
  ALU alu_1 (
    .rs(register_bank_1_read_data_1), .rt(multiplexer_5_out), .Sinal_Alu_Control(ALUcontrol),
    .Zero(alu_1_zero), .rd(alu_1_rd), .HI(HI), .LO(LO));
  Multiplexer #(.width(32)) multiplexer_6 (
    .in0(multiplexer_10_out), .in1({instruction_decode_1__15_0__shamt___funct, funct, {16{1'b0}}}),
    .out(multiplexer_6_out), .sel(LUI_2));  // open: en
  Multiplexer #(.width(32), .enable("false")) multiplexer_7 (
    .in0(adder_1_out), .in1(adder_2_out), .out(multiplexer_7_out), .sel(and_1_out));
  and and_1 (and_1_out, Branch_2, multiplexer_3_out);
  RAM #(.addrWidth(24), .dataWidth(32), .bus("separate")) ram_1 (
    .addr(alu_1_rd[25:2]), .din(register_bank_1_read_data_2), .data(ram_1_data), .str(MemWrite_2),
    .sel(1'b1), .clk(ck), .ld(MemRead_2), .clr(1'b0));
  Multiplexer #(.select(2), .width(32)) multiplexer_8 (
    .in0(multiplexer_7_out), .in1({adder_1_out[31:28], shl_26_28_1_out_2}),
    .in2({2'b00, shl_26_28_1_out_2[25:0], PC_q[31:28]}), .in3({32{1'b0}}), .out(multiplexer_8_out),
    .sel({WriteReg31_2, Jump_2}));  // open: en
  Multiplexer #(.select(2), .width(32)) multiplexer_9 (
    .in0(alu_1_rd), .in1(ram_1_data), .in2(adder_1_out), .in3({32{1'b0}}), .out(multiplexer_9_out),
    .sel({WriteReg31_2, MemToReg_2}));  // open: en
  BitSelector #(.width(32)) bitselector_1 (.in(multiplexer_9_out), .out(bitselector_1_out), .sel({5{1'b1}}));
  Register #(.width(32)) u_HI (.D(HI), .en(MULT), .clk(ck), .clr(Reset));  // open: Q
  Register #(.width(32)) u_LO (.D(LO), .en(MULT), .clk(ck), .clr(Reset));  // open: Q
  assign bit_extender_2_out = {{31{bitselector_1_out}}, bitselector_1_out};  // Bit_Extender bit_extender_2
  Multiplexer #(.width(32)) multiplexer_10 (
    .in0(multiplexer_9_out), .in1(and_2_out), .out(multiplexer_10_out), .sel(Slti_2));  // open: en
  Comparator #(.width(6), .mode("unsigned")) comparator_2 (.a(funct), .b(6'b011000), .eq(MULT));  // open: gt, lt
  Adder #(.width(32)) adder_3 (.a(32'h2), .b(bit_extender_2_out), .out(adder_3_out));  // open: cin, cout
  assign and_2_out = adder_3_out & 32'h1;  // AND_Gate and_2, 32 bits wide

  // Other names for the same wires on the sheet: É_MULT[5:0] = funct; rst = Reset

  // Notes on the sheet:
  //   BGEZ: Branch é definido por $rs >=0
  //   BEQ: Branch é definido pelo "zero" da ULA
  //   Bloco Operativo
  //   Bloco de Controle
  //   Instruction Memory
  //   contents of rom_1 (hex, n*v repeats v):
  //   241 e04 2 600 24 5*0 1320 4*0 2200 8*0 40 10*0 318 7*0 180
  //   contents of rom_2 (hex, n*v repeats v):
  //   c0e0070 8c020004 221820 621822 10610002 ac000008 8000000 ac030008 8000000
  //   SINAIS DE CONTROLE ADICIONADOS: WriteReg31, Bgez, Slti, LUI
  //   Inst 25-0
  //   zero (ula)
  //   $rs >= 0
  //   sinal bgez
  //   Shift Left 2
  //   Registers
  //   Sign Extend
  //   ALU Control
  //   Shift Left 2
  //   ALU
  //   Data Memory
  //   resultado ALU
  //   sinal Slti
  //   (utilizado no LUI)
  //   bit mais significativo da ALU
  //   -1, negativo; 0, positivo
  //   if ALU < 0: rt=1; else: rt=0
  //   soma cte 2
  //   pega valor imediato de 16 bits, coloca como os 16 bits mais significativos e completa os 16 bits menos significativos com zeros
  //   Registrador especial com os 32 bits mais significativos do resultado do MULT
  //   Registrador especial com os 32 bits menos significativos do resultado do MULT
  //   se o resultado da soma com cte 2 for 1,
  //   significa que o bit somado com a cte 2 era -1.
  //   Logo, o resultado deve ser 1, se não, 0.
endmodule

module Instruction_Decode (
  input  [31:0] in_1,
  output [5:0] _31_26__OPCODE,
  output [4:0] _25_21__RS,
  output [4:0] _20_16__RT,
  output [4:0] _15_11__RD,
  output [15:0] _15_0__SHAMT___FUNCT
);


  assign _15_0__SHAMT___FUNCT = in_1[15:0];
  assign _15_11__RD = in_1[15:11];
  assign _20_16__RT = in_1[20:16];
  assign _25_21__RS = in_1[25:21];
  assign _31_26__OPCODE = in_1[31:26];
endmodule

module Dec_5_1 (
  input  [4:0] in_1,
  output out_2,
  output out_3,
  output out_4,
  output out_5,
  output out_6,
  output out_7,
  output out_8,
  output out_9,
  output out_10,
  output out_11,
  output out_12,
  output out_13,
  output out_14,
  output out_15,
  output out_16,
  output out_17,
  output out_18,
  output out_19,
  output out_20,
  output out_21,
  output out_22,
  output out_23,
  output out_24,
  output out_25,
  output out_26,
  output out_27,
  output out_28,
  output out_29,
  output out_30,
  output out_31,
  output out_32,
  output out_33
);

  wire decoder_1_out0, decoder_2_out0, not_1_out, not_2_out, not_3_out, not_4_out;
  wire [3:0] and_1_out, and_5_out;

  not not_1 (not_1_out, in_1[4]);
  not not_2 (not_2_out, in_1[4]);
  not not_3 (not_3_out, in_1[4]);
  not not_4 (not_4_out, in_1[4]);
  and and_1 (and_1_out[0], not_1_out, in_1[0]);
  and and_2 (and_1_out[1], not_2_out, in_1[1]);
  and and_3 (and_1_out[2], not_3_out, in_1[2]);
  and and_4 (and_1_out[3], not_4_out, in_1[3]);
  and and_5 (and_5_out[0], in_1[4], in_1[0]);
  and and_6 (and_5_out[1], in_1[4], in_1[1]);
  and and_7 (and_5_out[2], in_1[4], in_1[2]);
  and and_8 (and_5_out[3], in_1[4], in_1[3]);
  Decoder #(.select(4), .enable("false")) decoder_1 (
    .out0(decoder_1_out0), .out1(out_3), .out2(out_4), .out3(out_5), .out4(out_6), .out5(out_7),
    .out6(out_8), .out7(out_9), .out8(out_10), .out9(out_11), .out10(out_12), .out11(out_13), .out12(out_14),
    .out13(out_15), .out14(out_16), .out15(out_17), .sel(and_1_out));
  Decoder #(.select(4), .enable("false")) decoder_2 (
    .out0(decoder_2_out0), .out1(out_19), .out2(out_20), .out3(out_21), .out4(out_22), .out5(out_23),
    .out6(out_24), .out7(out_25), .out8(out_26), .out9(out_27), .out10(out_28), .out11(out_29),
    .out12(out_30), .out13(out_31), .out14(out_32), .out15(out_33), .sel(and_5_out));
  and and_9 (out_2, not_1_out, decoder_1_out0);
  and and_10 (out_18, in_1[4], decoder_2_out0);
endmodule

module Register_Bank (
  input  [4:0] Read_1_Address,
  input  [4:0] Read_2_Address,
  input  [4:0] Write_Address,
  input  [31:0] Write_Data,
  input  Enable,
  input  Reset,
  input  Clock,
  output [31:0] Read_Data_1,
  output [31:0] Read_Data_2
);

  wire and_1_out, and_2_out, and_3_out, and_4_out, and_5_out, and_6_out, and_7_out, and_8_out, and_9_out,
       and_10_out, and_11_out, and_12_out, and_13_out, and_14_out, and_15_out, and_16_out, and_17_out,
       and_18_out, and_19_out, and_20_out, and_21_out, and_22_out, and_23_out, and_24_out, and_25_out,
       and_26_out, and_27_out, and_28_out, and_29_out, and_30_out, and_31_out, and_32_out, dec_5_1_1_out_2,
       dec_5_1_1_out_3, dec_5_1_1_out_4, dec_5_1_1_out_5, dec_5_1_1_out_6, dec_5_1_1_out_7, dec_5_1_1_out_8,
       dec_5_1_1_out_9, dec_5_1_1_out_10, dec_5_1_1_out_11, dec_5_1_1_out_12, dec_5_1_1_out_13,
       dec_5_1_1_out_14, dec_5_1_1_out_15, dec_5_1_1_out_16, dec_5_1_1_out_17, dec_5_1_1_out_18,
       dec_5_1_1_out_19, dec_5_1_1_out_20, dec_5_1_1_out_21, dec_5_1_1_out_22, dec_5_1_1_out_23,
       dec_5_1_1_out_24, dec_5_1_1_out_25, dec_5_1_1_out_26, dec_5_1_1_out_27, dec_5_1_1_out_28,
       dec_5_1_1_out_29, dec_5_1_1_out_30, dec_5_1_1_out_31, dec_5_1_1_out_32, dec_5_1_1_out_33;
  wire [31:0] multiplexer_1_out, multiplexer_2_out, multiplexer_3_out, multiplexer_4_out, register_2_q,
       register_3_q, register_4_q, register_5_q, register_6_q, register_7_q, register_8_q, register_9_q,
       register_10_q, register_11_q, register_12_q, register_13_q, register_14_q, register_15_q,
       register_16_q, register_17_q, register_18_q, register_19_q, register_20_q, register_21_q,
       register_22_q, register_23_q, register_24_q, register_25_q, register_26_q, register_27_q,
       register_28_q, register_29_q, register_30_q, register_31_q, register_32_q;

  Dec_5_1 dec_5_1_1 (
    .in_1(Write_Address), .out_2(dec_5_1_1_out_2), .out_3(dec_5_1_1_out_3), .out_4(dec_5_1_1_out_4),
    .out_5(dec_5_1_1_out_5), .out_6(dec_5_1_1_out_6), .out_7(dec_5_1_1_out_7), .out_8(dec_5_1_1_out_8),
    .out_9(dec_5_1_1_out_9), .out_10(dec_5_1_1_out_10), .out_11(dec_5_1_1_out_11), .out_12(dec_5_1_1_out_12),
    .out_13(dec_5_1_1_out_13), .out_14(dec_5_1_1_out_14), .out_15(dec_5_1_1_out_15),
    .out_16(dec_5_1_1_out_16), .out_17(dec_5_1_1_out_17), .out_18(dec_5_1_1_out_18),
    .out_19(dec_5_1_1_out_19), .out_20(dec_5_1_1_out_20), .out_21(dec_5_1_1_out_21),
    .out_22(dec_5_1_1_out_22), .out_23(dec_5_1_1_out_23), .out_24(dec_5_1_1_out_24),
    .out_25(dec_5_1_1_out_25), .out_26(dec_5_1_1_out_26), .out_27(dec_5_1_1_out_27),
    .out_28(dec_5_1_1_out_28), .out_29(dec_5_1_1_out_29), .out_30(dec_5_1_1_out_30),
    .out_31(dec_5_1_1_out_31), .out_32(dec_5_1_1_out_32), .out_33(dec_5_1_1_out_33));
  and and_1 (and_1_out, dec_5_1_1_out_2, Enable);
  and and_2 (and_2_out, dec_5_1_1_out_3, Enable);
  and and_3 (and_3_out, dec_5_1_1_out_4, Enable);
  and and_4 (and_4_out, dec_5_1_1_out_5, Enable);
  and and_5 (and_5_out, dec_5_1_1_out_6, Enable);
  and and_6 (and_6_out, dec_5_1_1_out_7, Enable);
  and and_7 (and_7_out, dec_5_1_1_out_8, Enable);
  and and_8 (and_8_out, dec_5_1_1_out_9, Enable);
  and and_9 (and_9_out, dec_5_1_1_out_10, Enable);
  and and_10 (and_10_out, dec_5_1_1_out_11, Enable);
  and and_11 (and_11_out, dec_5_1_1_out_12, Enable);
  and and_12 (and_12_out, dec_5_1_1_out_13, Enable);
  and and_13 (and_13_out, dec_5_1_1_out_14, Enable);
  and and_14 (and_14_out, dec_5_1_1_out_15, Enable);
  and and_15 (and_15_out, dec_5_1_1_out_16, Enable);
  and and_16 (and_16_out, dec_5_1_1_out_17, Enable);
  and and_17 (and_17_out, dec_5_1_1_out_18, Enable);
  and and_18 (and_18_out, dec_5_1_1_out_19, Enable);
  and and_19 (and_19_out, dec_5_1_1_out_20, Enable);
  and and_20 (and_20_out, dec_5_1_1_out_21, Enable);
  and and_21 (and_21_out, dec_5_1_1_out_22, Enable);
  and and_22 (and_22_out, dec_5_1_1_out_23, Enable);
  and and_23 (and_23_out, dec_5_1_1_out_24, Enable);
  and and_24 (and_24_out, dec_5_1_1_out_25, Enable);
  and and_25 (and_25_out, dec_5_1_1_out_26, Enable);
  and and_26 (and_26_out, dec_5_1_1_out_27, Enable);
  and and_27 (and_27_out, dec_5_1_1_out_28, Enable);
  and and_28 (and_28_out, dec_5_1_1_out_29, Enable);
  and and_29 (and_29_out, dec_5_1_1_out_30, Enable);
  and and_30 (and_30_out, dec_5_1_1_out_31, Enable);
  and and_31 (and_31_out, dec_5_1_1_out_32, Enable);
  and and_32 (and_32_out, dec_5_1_1_out_33, Enable);
  Register #(.width(32)) register_1 (.D(Write_Data), .en(and_1_out), .clk(Clock), .clr(Reset));  // open: Q
  Register #(.width(32)) register_2 (.D(Write_Data), .en(and_2_out), .Q(register_2_q), .clk(Clock), .clr(Reset));
  Register #(.width(32)) register_3 (.D(Write_Data), .en(and_3_out), .Q(register_3_q), .clk(Clock), .clr(Reset));
  Register #(.width(32)) register_4 (.D(Write_Data), .en(and_4_out), .Q(register_4_q), .clk(Clock), .clr(Reset));
  Register #(.width(32)) register_5 (.D(Write_Data), .en(and_5_out), .Q(register_5_q), .clk(Clock), .clr(Reset));
  Register #(.width(32)) register_6 (.D(Write_Data), .en(and_6_out), .Q(register_6_q), .clk(Clock), .clr(Reset));
  Register #(.width(32)) register_7 (.D(Write_Data), .en(and_7_out), .Q(register_7_q), .clk(Clock), .clr(Reset));
  Register #(.width(32)) register_8 (.D(Write_Data), .en(and_8_out), .Q(register_8_q), .clk(Clock), .clr(Reset));
  Register #(.width(32)) register_9 (.D(Write_Data), .en(and_9_out), .Q(register_9_q), .clk(Clock), .clr(Reset));
  Register #(.width(32)) register_10 (.D(Write_Data), .en(and_10_out), .Q(register_10_q), .clk(Clock), .clr(Reset));
  Register #(.width(32)) register_11 (.D(Write_Data), .en(and_11_out), .Q(register_11_q), .clk(Clock), .clr(Reset));
  Register #(.width(32)) register_12 (.D(Write_Data), .en(and_12_out), .Q(register_12_q), .clk(Clock), .clr(Reset));
  Register #(.width(32)) register_13 (.D(Write_Data), .en(and_13_out), .Q(register_13_q), .clk(Clock), .clr(Reset));
  Register #(.width(32)) register_14 (.D(Write_Data), .en(and_14_out), .Q(register_14_q), .clk(Clock), .clr(Reset));
  Register #(.width(32)) register_15 (.D(Write_Data), .en(and_15_out), .Q(register_15_q), .clk(Clock), .clr(Reset));
  Register #(.width(32)) register_16 (.D(Write_Data), .en(and_16_out), .Q(register_16_q), .clk(Clock), .clr(Reset));
  Register #(.width(32)) register_17 (.D(Write_Data), .en(and_17_out), .Q(register_17_q), .clk(Clock), .clr(Reset));
  Register #(.width(32)) register_18 (.D(Write_Data), .en(and_18_out), .Q(register_18_q), .clk(Clock), .clr(Reset));
  Register #(.width(32)) register_19 (.D(Write_Data), .en(and_19_out), .Q(register_19_q), .clk(Clock), .clr(Reset));
  Register #(.width(32)) register_20 (.D(Write_Data), .en(and_20_out), .Q(register_20_q), .clk(Clock), .clr(Reset));
  Register #(.width(32)) register_21 (.D(Write_Data), .en(and_21_out), .Q(register_21_q), .clk(Clock), .clr(Reset));
  Register #(.width(32)) register_22 (.D(Write_Data), .en(and_22_out), .Q(register_22_q), .clk(Clock), .clr(Reset));
  Register #(.width(32)) register_23 (.D(Write_Data), .en(and_23_out), .Q(register_23_q), .clk(Clock), .clr(Reset));
  Register #(.width(32)) register_24 (.D(Write_Data), .en(and_24_out), .Q(register_24_q), .clk(Clock), .clr(Reset));
  Register #(.width(32)) register_25 (.D(Write_Data), .en(and_25_out), .Q(register_25_q), .clk(Clock), .clr(Reset));
  Register #(.width(32)) register_26 (.D(Write_Data), .en(and_26_out), .Q(register_26_q), .clk(Clock), .clr(Reset));
  Register #(.width(32)) register_27 (.D(Write_Data), .en(and_27_out), .Q(register_27_q), .clk(Clock), .clr(Reset));
  Register #(.width(32)) register_28 (.D(Write_Data), .en(and_28_out), .Q(register_28_q), .clk(Clock), .clr(Reset));
  Register #(.width(32)) register_29 (.D(Write_Data), .en(and_29_out), .Q(register_29_q), .clk(Clock), .clr(Reset));
  Register #(.width(32)) register_30 (.D(Write_Data), .en(and_30_out), .Q(register_30_q), .clk(Clock), .clr(Reset));
  Register #(.width(32)) register_31 (.D(Write_Data), .en(and_31_out), .Q(register_31_q), .clk(Clock), .clr(Reset));
  Register #(.width(32)) register_32 (.D(Write_Data), .en(and_32_out), .Q(register_32_q), .clk(Clock), .clr(Reset));
  Multiplexer #(.select(4), .width(32), .enable("false")) multiplexer_1 (
    .in0({32{1'b0}}), .in1(register_2_q), .in2(register_3_q), .in3(register_4_q), .in4(register_5_q),
    .in5(register_6_q), .in6(register_7_q), .in7(register_8_q), .in8(register_9_q), .in9(register_10_q),
    .in10(register_11_q), .in11(register_12_q), .in12(register_13_q), .in13(register_14_q),
    .in14(register_15_q), .in15(register_16_q), .out(multiplexer_1_out), .sel(Read_2_Address[3:0]));
  Multiplexer #(.select(4), .width(32), .enable("false")) multiplexer_2 (
    .in0({32{1'b0}}), .in1(register_2_q), .in2(register_3_q), .in3(register_4_q), .in4(register_5_q),
    .in5(register_6_q), .in6(register_7_q), .in7(register_8_q), .in8(register_9_q), .in9(register_10_q),
    .in10(register_11_q), .in11(register_12_q), .in12(register_13_q), .in13(register_14_q),
    .in14(register_15_q), .in15(register_16_q), .out(multiplexer_2_out), .sel(Read_1_Address[3:0]));
  Multiplexer #(.select(4), .width(32), .enable("false")) multiplexer_3 (
    .in0(register_17_q), .in1(register_18_q), .in2(register_19_q), .in3(register_20_q), .in4(register_21_q),
    .in5(register_22_q), .in6(register_23_q), .in7(register_24_q), .in8(register_25_q), .in9(register_26_q),
    .in10(register_27_q), .in11(register_28_q), .in12(register_29_q), .in13(register_30_q),
    .in14(register_31_q), .in15(register_32_q), .out(multiplexer_3_out), .sel(Read_1_Address[3:0]));
  Multiplexer #(.select(4), .width(32), .enable("false")) multiplexer_4 (
    .in0(register_17_q), .in1(register_18_q), .in2(register_19_q), .in3(register_20_q), .in4(register_21_q),
    .in5(register_22_q), .in6(register_23_q), .in7(register_24_q), .in8(register_25_q), .in9(register_26_q),
    .in10(register_27_q), .in11(register_28_q), .in12(register_29_q), .in13(register_30_q),
    .in14(register_31_q), .in15(register_32_q), .out(multiplexer_4_out), .sel(Read_2_Address[3:0]));
  Multiplexer #(.width(32), .enable("false")) multiplexer_5 (
    .in0(multiplexer_2_out), .in1(multiplexer_3_out), .out(Read_Data_1), .sel(Read_1_Address[4]));
  Multiplexer #(.width(32), .enable("false")) multiplexer_6 (
    .in0(multiplexer_1_out), .in1(multiplexer_4_out), .out(Read_Data_2), .sel(Read_2_Address[4]));
endmodule

module ALU (
  input  [31:0] rs,
  input  [31:0] rt,
  input  [2:0] Sinal_Alu_Control,
  output Zero,
  output [31:0] rd,
  output [31:0] HI,
  output [31:0] LO
);

  wire or_2_out, or_3_out, or_4_out, or_5_out, or_6_out;
  wire [31:0] adder_1_out, and_1_out, or_1_out, subtractor_1_out;

  assign and_1_out = rs & rt;  // AND_Gate and_1, 32 bits wide
  assign or_1_out = rs | rt;  // OR_Gate or_1, 32 bits wide
  Adder #(.width(32)) adder_1 (.a(rs), .b(rt), .out(adder_1_out));  // open: cin, cout
  Multiplier #(.width(32)) multiplier_1 (.a(rs), .b(rt), .out(LO), .cout(HI));  // open: cin
  Subtractor #(.width(32)) subtractor_1 (.a(rs), .b(rt), .out(subtractor_1_out));  // open: bin, bout
  Multiplexer #(.select(3), .width(32), .enable("false")) multiplexer_1 (
    .in0(and_1_out), .in1(or_1_out), .in2(adder_1_out), .in3(LO), .in6(subtractor_1_out),
    .in7({{31{1'b0}}, subtractor_1_out[31]}), .out(rd), .sel(Sinal_Alu_Control));  // open: in4, in5
  or or_2 (or_2_out, rd[0], rd[1], rd[2], rd[3], rd[4], rd[5], rd[6], rd[7], rd[8]);
  or or_3 (or_3_out, rd[9], rd[10], rd[11], rd[12], rd[13], rd[14], rd[15], rd[16], rd[17]);
  or or_4 (or_4_out, rd[18], rd[19], rd[20], rd[21], rd[22], rd[23], rd[24], rd[25], rd[26]);
  or or_5 (or_5_out, rd[27], rd[28], rd[29], rd[30], rd[31]);
  or or_6 (or_6_out, or_2_out, or_3_out, or_4_out, or_5_out);
  not not_1 (Zero, or_6_out);

  // Other names for the same wires on the sheet: MULT_HI[31:0] = HI; MULT_LO[31:0] = LO
endmodule

module shl_26_28 (
  input  [25:0] in_1,
  output [27:0] out_2
);


  assign out_2 = {in_1, 2'b00};
endmodule

module merge_PC (
  input  [27:0] in_1,
  input  [3:0] in_2,
  output [31:0] out_3
);


  assign out_3 = {in_2, in_1};
endmodule

module sig_ext (
  input  [15:0] in_1,
  output [31:0] out_2
);


  assign out_2 = {{17{in_1[15]}}, in_1[14:0]};
endmodule

module shl_32 (
  input  [31:0] in_1,
  output [31:0] out_2
);


  assign out_2 = {in_1[29:0], 2'b00};
endmodule

module ALU_Control (
  input  [1:0] in_1,
  input  [4:0] in_2,
  output [2:0] out_3
);

  wire and_1_out, not_1_out, not_2_out, or_1_out;

  and and_1 (and_1_out, in_1[1], in_2[1]);
  not not_1 (not_1_out, in_1[1]);
  not not_2 (not_2_out, in_2[2]);
  or or_1 (or_1_out, in_2[3], in_2[0]);
  or or_2 (out_3[1], not_1_out, not_2_out);
  and and_2 (out_3[0], in_1[1], or_1_out);
  or or_3 (out_3[2], in_1[0], and_1_out);
endmodule

module Debug_Register_Bank (
  input  Debug,
  input  Debug_Enable,
  input  [4:0] Debug_Write_Address,
  input  [31:0] Debug_Write_Data,
  input  [4:0] Read_1_Address,
  input  [4:0] Read_2_Address,
  input  [4:0] Write_Address,
  input  [31:0] Write_Data,
  input  Enable,
  input  Reset,
  input  Clock,
  output [31:0] Read_Data_1,
  output [31:0] Read_Data_2
);

  wire and_1_out, not_1_out, or_1_out;
  wire [4:0] multiplexer_1_out;
  wire [31:0] multiplexer_2_out;

  not not_1 (not_1_out, Debug);
  Multiplexer #(.width(5), .enable("false")) multiplexer_1 (
    .in0(Write_Address), .in1(Debug_Write_Address), .out(multiplexer_1_out), .sel(Debug));
  Multiplexer #(.width(32), .enable("false")) multiplexer_2 (
    .in0(Write_Data), .in1(Debug_Write_Data), .out(multiplexer_2_out), .sel(Debug));
  or or_1 (or_1_out, Debug_Enable, Enable);
  and and_1 (and_1_out, not_1_out, Reset);
  Register_Bank register_bank_1 (
    .Read_1_Address(Read_1_Address), .Read_2_Address(Read_2_Address), .Write_Address(multiplexer_1_out),
    .Write_Data(multiplexer_2_out), .Enable(or_1_out), .Reset(and_1_out), .Clock(Clock),
    .Read_Data_1(Read_Data_1), .Read_Data_2(Read_Data_2));
endmodule
